// Logisim project Proj.circ as structural Verilog: 2 circuits, main circuit main
module main (
);

  wire _0, _1, _2, _3, _4, _5, _6, _7, _8, _9, and_1_out, C, comparator_1_eq, comparator_2_eq,
       comparator_3_lt, counter_1_carry, counter_2_carry, d_ff_1_q, d_ff_2_q, demultiplexer_1_out0,
       demultiplexer_1_out1, F, nor_1_out, nor_2_out, nor_3_out, nor_4_out, nor_5_out, nor_6_out, not_1_out,
       not_2_out, not_3_out, not_4_out, not_5_out, not_6_out, or_1_out, or_6_out, or_7_out, or_8_out,
       or_9_out, pull_resistor_1_node, pull_resistor_3_node;
  wire [3:0] controlled_buffer_1_out, controlled_buffer_2_out, counter_1_q, counter_2_q,
       demultiplexer_2_out1, demultiplexer_2_out2, demultiplexer_2_out3, demultiplexer_2_out4,
       demultiplexer_2_out5, demultiplexer_2_out6, multiplexer_1_out, or_2_out, ram_1_data, ram_2_data,
       register_1_q, register_2_q, register_3_q, register_4_q, register_5_q, register_6_q, register_7_q,
       register_8_q;

  LED Locked (.in(d_ff_1_q));
  D_Flip_Flop d_ff_1 (.clk(and_1_out), .D(and_1_out), .Q(d_ff_1_q), .reset(or_1_out));  // open: Qn, preset, en
  or or_1 (or_1_out, C, counter_2_carry);
  and and_1 (and_1_out, d_ff_2_q, comparator_1_eq);
  Button u__2 (.out(_2));
  Button u__1 (.out(_1));
  Button u__4 (.out(_4));
  Button u__5 (.out(_5));
  Button u__7 (.out(_7));
  Button u__8 (.out(_8));
  Button u__0 (.out(_0));
  Comparator #(.width(4)) comparator_1 (.a(4'b0000), .b(counter_1_q), .eq(comparator_1_eq));  // open: gt, lt
  Counter #(.width(4), .max('h7), .ongoal("load")) counter_1 (
    .Q(counter_1_q), .carry(counter_1_carry), .clk(or_6_out), .clr(C));  // open: load, D, count
  or or_2 (or_2_out[0], _1, _3, _5, _7, _9);
  or or_3 (or_2_out[1], _2, _3, _6, _7);
  or or_4 (or_2_out[2], _4, _5, _6, _7);
  or or_5 (or_2_out[3], _8, _9);
  Button u__3 (.out(_3));
  Button u__6 (.out(_6));
  Button u__9 (.out(_9));
  Button CLEAR (.out(C));
  D_Flip_Flop d_ff_2 (.clk(counter_1_carry), .D(counter_1_carry), .Q(d_ff_2_q), .reset(C));  // open: Qn, preset, en
  or or_6 (or_6_out, _0, or_2_out[0], or_2_out[1], or_2_out[2], or_2_out[3]);
  Button u_F (.out(F));
  not not_1 (not_1_out, or_6_out);
  Demultiplexer #(.enable("false")) demultiplexer_1 (
    .out0(demultiplexer_1_out0), .out1(demultiplexer_1_out1), .in(not_1_out), .sel(d_ff_2_q));
  Register #(.width(4), .trigger("high")) register_1 (.D(or_2_out), .Q(register_1_q), .clk(or_6_out));  // open: en, clr
  not not_2 (not_2_out, counter_1_q[2]);
  not not_3 (not_3_out, counter_1_q[1]);
  RAM #(.addrWidth(4), .dataWidth(4), .bus("separate")) ram_1 (
    .addr(counter_1_q), .din(register_1_q), .data(ram_1_data), .clk(demultiplexer_1_out1), .clr(C));  // open: str, sel, ld
  RAM #(.addrWidth(4), .dataWidth(4), .bus("separate")) ram_2 (
    .addr(counter_1_q), .din(register_1_q), .data(ram_2_data), .clk(demultiplexer_1_out0), .clr(C));  // open: str, sel, ld
  not not_4 (not_4_out, counter_1_q[2]);
  assign controlled_buffer_1_out = d_ff_1_q ? counter_1_q : 4'bz;  // Controlled_Buffer controlled_buffer_1
  assign controlled_buffer_2_out = d_ff_1_q ? counter_2_q : 4'bz;  // Controlled_Buffer controlled_buffer_2
  Comparator #(.width(4)) comparator_2 (.a(ram_1_data), .b(ram_2_data), .eq(comparator_2_eq));  // open: gt, lt
  Demultiplexer #(.select(4), .width(4), .tristate("true"), .disabled(0), .enable("false")) demultiplexer_2 (
    .out1(demultiplexer_2_out1), .out2(demultiplexer_2_out2), .out3(demultiplexer_2_out3),
    .out4(demultiplexer_2_out4), .out5(demultiplexer_2_out5), .out6(demultiplexer_2_out6), .in(register_2_q),
    .sel(counter_1_q));  // open: out0, out7, out8, out9, out10, out11, out12, out13, out14, out15
  Register #(.width(4), .trigger("high")) register_2 (
    .D(multiplexer_1_out), .Q(register_2_q), .clk(not_1_out));  // open: en, clr
  Multiplexer #(.width(4), .enable("false")) multiplexer_1 (
    .in0(ram_2_data), .in1(ram_1_data), .out(multiplexer_1_out), .sel(d_ff_2_q));
  nor nor_1 (nor_1_out, counter_1_q[0], not_3_out, not_2_out, counter_1_q[3]);
  not not_5 (not_5_out, counter_1_q[0]);
  nor nor_2 (nor_2_out, counter_1_q[0], not_3_out, counter_1_q[2], counter_1_q[3]);
  nor nor_3 (nor_3_out, not_5_out, not_3_out, counter_1_q[2], counter_1_q[3]);
  Pull_Resistor pull_resistor_1 (.node(pull_resistor_1_node));
  Comparator #(.width(4)) comparator_3 (
    .a(controlled_buffer_1_out), .b(controlled_buffer_2_out), .gt(pull_resistor_1_node), .lt(comparator_3_lt));  // open: eq
  Pull_Resistor pull_resistor_2 (.node(comparator_3_lt));
  Counter #(.width(4), .max('h6), .ongoal("stay")) counter_2 (
    .count(comparator_2_eq), .Q(counter_2_q), .carry(counter_2_carry), .clk(comparator_2_eq), .clr(or_7_out));  // open: load, D
  LED Correct_code (.in(counter_2_carry));
  or or_7 (or_7_out, counter_1_carry, C);
  nor nor_4 (nor_4_out, counter_1_q[1], not_5_out, counter_1_q[2], counter_1_q[3]);
  nor nor_5 (nor_5_out, counter_1_q[0], counter_1_q[1], not_4_out, counter_1_q[3]);
  nor nor_6 (nor_6_out, not_5_out, counter_1_q[1], not_4_out, counter_1_q[3]);
  Pull_Resistor pull_resistor_3 (.node(pull_resistor_3_node));
  or or_8 (or_8_out, pull_resistor_1_node, comparator_3_lt);
  assign pull_resistor_3_node = not_6_out ? or_8_out : 1'bz;  // Controlled_Buffer controlled_buffer_3
  not not_6 (not_6_out, or_6_out);
  Hex_Digit_Display hex_digit_display_1 (.value(register_4_q));  // open: dp
  or or_9 (or_9_out, comparator_1_eq, C);
  Register #(.width(4), .trigger("high")) register_3 (
    .D(demultiplexer_2_out6), .en(1'b1), .Q(register_3_q), .clk(nor_1_out), .clr(or_9_out));
  Register #(.width(4), .trigger("high")) register_4 (
    .D(demultiplexer_2_out1), .en(1'b1), .Q(register_4_q), .clk(nor_4_out), .clr(or_9_out));
  Register #(.width(4), .trigger("high")) register_5 (
    .D(demultiplexer_2_out2), .en(1'b1), .Q(register_5_q), .clk(nor_2_out), .clr(or_9_out));
  Hex_Digit_Display hex_digit_display_2 (.value(register_5_q));  // open: dp
  Hex_Digit_Display hex_digit_display_3 (.value(register_6_q));  // open: dp
  Counter #(.width(4), .max('h4), .ongoal("stay")) counter_3 (
    .count(pull_resistor_3_node), .clk(pull_resistor_3_node), .clr(C));  // open: load, D, Q, carry
  Hex_Digit_Display hex_digit_display_4 (.value(register_7_q));  // open: dp
  Register #(.width(4), .trigger("high")) register_6 (
    .D(demultiplexer_2_out3), .en(1'b1), .Q(register_6_q), .clk(nor_3_out), .clr(or_9_out));
  Register #(.width(4), .trigger("high")) register_7 (
    .D(demultiplexer_2_out4), .en(1'b1), .Q(register_7_q), .clk(nor_5_out), .clr(or_9_out));
  Hex_Digit_Display hex_digit_display_5 (.value(register_3_q));  // open: dp
  Hex_Digit_Display hex_digit_display_6 (.value(register_8_q));  // open: dp
  Register #(.width(4), .trigger("high")) register_8 (
    .D(demultiplexer_2_out5), .en(1'b1), .Q(register_8_q), .clk(nor_6_out), .clr(or_9_out));
endmodule

module _4bit_Latch (
  input  [3:0] in_1,
  input  in_2,
  input  in_3,
  input  [3:0] in_4,
  output out_5
);

  wire and_1_out, and_2_out, nor_2_out, not_1_out;

  not not_1 (not_1_out, in_3);
  and and_1 (and_1_out, not_1_out, in_2);
  and and_2 (and_2_out, in_3, in_2);
  nor nor_1 (out_5, and_1_out, nor_2_out);
  nor nor_2 (nor_2_out, out_5, and_2_out);
endmodule
